// Digital circuit VendMachine.dig as structural Verilog
module VendMachine (
  input  C,
  output Z_2,
  output Z_1,
  output Z_0,
  output co,
  output \do ,
  output no
);

  wire ACC_0, ACC_1, ACC_2, ACC_3, and_1_out, and_2_out, and_3_out, and_4_out, and_5_out, and_6_out,
       and_7_out, and_8_out, and_9_out, and_10_out, and_11_out, and_12_out, and_13_out, and_14_out,
       and_15_out, and_16_out, btn, d_ff_as_1_nq, di, enable, multiplexer_2_out, multiplexer_3_out,
       multiplexer_4_out, multiplexer_5_out, ni, not_1_out, not_2_out, not_3_out, not_4_out, not_5_out,
       not_6_out, not_7_out, not_8_out, or_1_out, or_2_out, or_3_out, qi, rst, SUM_0_c_o, SUM_0_s, SUM_1_c_o,
       SUM_1_s, SUM_2_c_o, SUM_2_s, SUM_3_s;
  wire [3:0] multiplexer_1_out, multiplexer_6_out, multiplexer_7_out, multiplexer_8_out, multiplexer_9_out;

  not not_1 (not_1_out, ni);
  not not_2 (not_2_out, di);
  DipSwitch Nickel (.out(ni));
  DipSwitch Dime (.out(di));
  DipSwitch Quarter (.out(qi));
  not not_3 (not_3_out, ACC_3);
  Button Button (.out(btn));
  Button Reset (.out(rst));
  not not_4 (not_4_out, ACC_1);
  not not_5 (not_5_out, ACC_2);
  not not_6 (not_6_out, Z_2);
  not not_7 (not_7_out, Z_1);
  not not_8 (not_8_out, Z_0);
  and and_1 (and_1_out, not_4_out, not_5_out, ACC_3, not_8_out, not_7_out, not_6_out);
  and and_2 (and_2_out, ACC_1, ACC_2, not_3_out, not_8_out, not_7_out, not_6_out);
  and and_3 (and_3_out, ACC_0, not_4_out, not_5_out, ACC_3, not_8_out, not_7_out);
  and and_4 (and_4_out, ACC_0, ACC_2, not_3_out, not_8_out, not_7_out);
  and and_5 (and_5_out, ACC_2, ACC_0);
  and and_6 (and_6_out, ACC_2, ACC_1);
  or or_1 (or_1_out, ni, qi);
  and and_7 (and_7_out, not_1_out, not_2_out, qi);
  and and_8 (and_8_out, Z_0, not_6_out);
  and and_9 (and_9_out, Z_0, Z_1);
  and and_10 (and_10_out, Z_0, Z_2);
  and and_11 (and_11_out, not_8_out, Z_1);
  and and_12 (and_12_out, not_8_out, Z_2);
  or or_2 (or_2_out, and_3_out, and_4_out, Z_2);
  or or_3 (or_3_out, ACC_3, and_5_out, and_6_out);
  and and_13 (and_13_out, enable, or_1_out);
  and and_14 (and_14_out, enable, not_1_out, di);
  and and_15 (and_15_out, enable, and_7_out);
  or or_4 (co, and_8_out, Z_1);
  or or_5 (\do , and_9_out, and_10_out);
  or or_6 (no, and_11_out, and_12_out);
  Add SUM_0 (.a(ACC_0), .b(and_13_out), .c_i(1'b0), .s(SUM_0_s), .c_o(SUM_0_c_o));
  Add SUM_1 (.a(ACC_1), .b(and_14_out), .c_i(SUM_0_c_o), .s(SUM_1_s), .c_o(SUM_1_c_o));
  Add SUM_2 (.a(ACC_2), .b(and_15_out), .c_i(SUM_1_c_o), .s(SUM_2_s), .c_o(SUM_2_c_o));
  Add SUM_3 (.a(ACC_3), .b(1'b0), .c_i(SUM_2_c_o), .s(SUM_3_s));  // open: c_o
  and and_16 (and_16_out, not_8_out, not_7_out, not_6_out);
  Seven_Seg_Hex seven_seg_hex_1 (.d(multiplexer_1_out), .dp(1'b0));
  Seven_Seg seven_seg_1 (.a(1'b0), .b(1'b0), .c(1'b0), .d(1'b0), .e(1'b0), .f(1'b0), .g(1'b0), .dp(1'b0));
  Multiplexer #(.Bits(4)) multiplexer_1 (.sel(co), .in_0(4'b0000), .in_1(4'b0001), .out(multiplexer_1_out));
  Multiplexer multiplexer_2 (.sel(or_3_out), .in_0(SUM_0_s), .in_1(not_5_out), .out(multiplexer_2_out));
  Multiplexer multiplexer_3 (.sel(or_3_out), .in_0(SUM_1_s), .in_1(not_5_out), .out(multiplexer_3_out));
  Multiplexer multiplexer_4 (.sel(or_3_out), .in_0(SUM_2_s), .in_1(not_5_out), .out(multiplexer_4_out));
  Multiplexer multiplexer_5 (.sel(or_3_out), .in_0(SUM_3_s), .in_1(1'b0), .out(multiplexer_5_out));
  Seven_Seg_Hex seven_seg_hex_2 (.d(multiplexer_6_out), .dp(1'b0));
  Multiplexer #(.Bits(4)) multiplexer_6 (.sel(\do ), .in_0(4'b0000), .in_1(4'b0001), .out(multiplexer_6_out));
  D_FF_AS Z_2_n (.Set(1'b0), .D(and_1_out), .C(C), .Clr(rst), .Q(Z_2));  // open: nQ
  D_FF_AS Z_1_n (.Set(1'b0), .D(and_2_out), .C(C), .Clr(rst), .Q(Z_1));  // open: nQ
  D_FF_AS Z_0_n (.Set(1'b0), .D(or_2_out), .C(C), .Clr(rst), .Q(Z_0));  // open: nQ
  D_FF_AS u_ACC_0 (.Set(1'b0), .D(multiplexer_2_out), .C(C), .Clr(rst), .Q(ACC_0));  // open: nQ
  D_FF_AS u_ACC_1 (.Set(1'b0), .D(multiplexer_3_out), .C(C), .Clr(rst), .Q(ACC_1));  // open: nQ
  D_FF_AS u_ACC_2 (.Set(1'b0), .D(multiplexer_4_out), .C(C), .Clr(rst), .Q(ACC_2));  // open: nQ
  D_FF_AS u_ACC_3 (.Set(1'b0), .D(multiplexer_5_out), .C(C), .Clr(rst), .Q(ACC_3));  // open: nQ
  D_FF_AS d_ff_as_1 (.Set(1'b0), .D(btn), .C(C), .Clr(rst), .nQ(d_ff_as_1_nq));  // open: Q
  Seven_Seg_Hex seven_seg_hex_3 (.d(multiplexer_7_out), .dp(1'b0));
  and and_17 (enable, and_16_out, d_ff_as_1_nq, btn);
  Seven_Seg_Hex seven_seg_hex_4 (.d(multiplexer_8_out), .dp(1'b0));
  Multiplexer #(.Bits(4)) multiplexer_7 (.sel(no), .in_0(4'b0000), .in_1(4'b0101), .out(multiplexer_7_out));
  Multiplexer #(.Selector_Bits(3), .Bits(4)) multiplexer_8 (
    .sel({ACC_3, ACC_2, ACC_1}), .in_0(4'b0000), .in_1(4'b0001), .in_2(4'b0010), .in_3(4'b0011),
    .in_4(4'b0100), .in_5(4'b0000), .in_6(4'b0000), .in_7(4'b0000), .out(multiplexer_8_out));
  Seven_Seg_Hex seven_seg_hex_5 (.d(multiplexer_9_out), .dp(1'b0));
  // Probe VendMachine.fsm on {ACC_3, ACC_2, ACC_1, ACC_0, Z_2, Z_1, Z_0}
  Multiplexer #(.Bits(4)) multiplexer_9 (.sel(ACC_0), .in_0(4'b0000), .in_1(4'b0101), .out(multiplexer_9_out));

  // Other names for the same wires on the sheet: Z_0_n = Z_0; Z_1_n = Z_1; Z_2_n = Z_2
endmodule
