// Digital circuit VendingMachine.dig as structural Verilog
module VendingMachine (
  input  di,
  input  ni,
  input  qi,
  input  C,
  output co,
  output \do ,
  output no
);

  wire and_1_out, and_2_out, and_3_out, and_4_out, and_5_out, and_6_out, and_7_out, and_8_out, and_9_out,
       and_10_out, and_11_out, and_12_out, and_13_out, and_14_out, and_15_out, and_16_out, and_17_out,
       and_18_out, and_19_out, and_20_out, and_21_out, and_22_out, and_23_out, and_24_out, and_25_out,
       and_26_out, and_27_out, and_28_out, D_5, not_1_out, not_2_out, not_3_out, not_4_out, not_5_out,
       not_6_out, or_1_out, or_5_out, or_6_out, or_7_out, Z_1_n, Z_2_n, Z_3_n;

  not not_1 (not_1_out, di);
  not not_2 (not_2_out, ni);
  not not_3 (not_3_out, qi);
  not not_4 (not_4_out, Z_2_n);
  not not_5 (not_5_out, Z_1_n);
  not not_6 (not_6_out, D_5);
  and and_1 (and_1_out, D_5, Z_1_n, not_4_out, not_1_out, not_2_out, qi);
  and and_2 (and_2_out, not_6_out, not_5_out, Z_2_n, not_1_out, not_2_out, qi);
  and and_3 (and_3_out, not_6_out, not_4_out, not_1_out, not_2_out, qi);
  and and_4 (and_4_out, not_6_out, not_5_out, Z_2_n, not_3_out);
  and and_5 (and_5_out, D_5, Z_1_n, not_4_out, ni);
  and and_6 (and_6_out, not_6_out, not_5_out, Z_2_n, ni);
  and and_7 (and_7_out, not_6_out, not_5_out, Z_2_n, di);
  and and_8 (and_8_out, not_5_out, not_4_out, not_1_out, not_2_out, qi);
  and and_9 (and_9_out, Z_1_n, not_4_out, di, not_2_out);
  and and_10 (and_10_out, D_5, not_5_out, not_4_out, qi);
  and and_11 (and_11_out, not_6_out, not_5_out, di, not_2_out);
  and and_12 (and_12_out, D_5, not_5_out, not_4_out, ni);
  and and_13 (and_13_out, not_6_out, Z_1_n, not_4_out, ni);
  and and_14 (and_14_out, not_6_out, Z_1_n, not_4_out, not_1_out);
  and and_15 (and_15_out, Z_1_n, not_4_out, not_1_out, not_2_out, not_3_out);
  and and_16 (and_16_out, not_5_out, not_4_out, di, not_2_out);
  and and_17 (and_17_out, D_5, not_4_out, not_2_out, not_3_out);
  and and_18 (and_18_out, not_6_out, not_5_out, not_1_out, qi);
  and and_19 (and_19_out, not_6_out, not_4_out, not_1_out, qi);
  and and_20 (and_20_out, D_5, not_4_out, di, not_2_out);
  and and_21 (and_21_out, not_6_out, not_5_out, ni);
  and and_22 (and_22_out, not_6_out, not_4_out, ni);
  and and_23 (and_23_out, D_5, Z_2_n);
  and and_24 (and_24_out, Z_1_n, Z_2_n);
  and and_25 (and_25_out, D_5, Z_1_n, Z_2_n);
  and and_26 (and_26_out, D_5, Z_3_n);
  and and_27 (and_27_out, not_6_out, Z_1_n, Z_2_n);
  and and_28 (and_28_out, not_6_out, Z_3_n);
  or or_1 (or_1_out, and_1_out, and_2_out);
  or or_2 (co, and_23_out, and_24_out);
  or or_3 (\do , and_25_out, and_26_out);
  or or_4 (no, and_27_out, and_28_out);
  or or_5 (or_5_out, and_3_out, and_4_out, and_5_out, and_6_out, and_7_out, and_8_out, and_9_out, Z_3_n);
  or or_6 (or_6_out, and_10_out, and_11_out, and_12_out, and_13_out, and_14_out, and_15_out, and_16_out, Z_3_n);
  or or_7 (or_7_out, and_17_out, and_18_out, and_19_out, and_20_out, and_21_out, and_22_out, Z_3_n);
  D_FF u_Z_3_n (.D(or_1_out), .C(C), .Q(Z_3_n));  // open: nQ
  D_FF u_Z_2_n (.D(or_5_out), .C(C), .Q(Z_2_n));  // open: nQ
  D_FF u_Z_1_n (.D(or_6_out), .C(C), .Q(Z_1_n));  // open: nQ
  D_FF Z_0_n (.D(or_7_out), .C(C), .Q(D_5));  // open: nQ
  // Probe VendingMachine.fsm on {qi, ni, di, Z_3_n, Z_2_n, Z_1_n, D_5}

  // Other names for the same wires on the sheet: Z_0_n = D_5
endmodule
